// Logisim project d-flip-flop.circ as structural Verilog: 1 circuit, main circuit main
module main (
  input  D,
  output Q,
  output nQ
);

  wire clock_1_out, main_1_q, not_1_out;

  Clock clock_1 (.out(clock_1_out));
  d_latch_withoutclock_main main_1 (.C(clock_1_out), .D(D), .Q(main_1_q));  // open: nQ
  not not_1 (not_1_out, clock_1_out);
  d_latch_withoutclock_main main_2 (.C(not_1_out), .D(main_1_q), .Q(Q), .nQ(nQ));

  // Notes on the sheet:
  //   C
endmodule
