// Logisim project 03 Lab.circ as structural Verilog: 1 circuit, main circuit main
module main (
  input  [1:0] in_1,
  output [1:0] \output 
);

  wire clock_1_out;

  Clock clock_1 (.out(clock_1_out));
  d_flip_flop_withoutclock_main main_1 (.C(clock_1_out), .D(in_1[1]), .Q(\output [1]));  // open: nQ
  d_flip_flop_withoutclock_main main_2 (.C(clock_1_out), .D(in_1[0]), .Q(\output [0]));  // open: nQ

  // Notes on the sheet:
  //   C
  //   input
endmodule
