// Logisim project Multiplexer.circ as structural Verilog: 1 circuit, main circuit main
module main (
  input  in_1,
  input  in_2,
  input  A,
  input  B,
  input  S2,
  input  S1,
  output out_7
);

  wire and_1_out, and_2_out, and_3_out, and_4_out, not_1_out;

  not not_1 (not_1_out, S2);
  and and_1 (and_1_out, in_1, not_1_out);
  and and_2 (and_2_out, in_2, not_1_out);
  and and_3 (and_3_out, A, S2);
  and and_4 (and_4_out, S2, B);
  or or_1 (out_7, and_1_out, and_2_out, and_3_out, and_4_out);
endmodule
