// Logisim project d-flip-flop-withoutclock.circ as structural Verilog: 1 circuit, main circuit main
module main (
  input  C,
  input  D,
  output Q,
  output nQ
);

  wire main_1_q, not_1_out;

  d_latch_withoutclock_main main_1 (.C(C), .D(D), .Q(main_1_q));  // open: nQ
  not not_1 (not_1_out, C);
  d_latch_withoutclock_main main_2 (.C(not_1_out), .D(main_1_q), .Q(Q), .nQ(nQ));
endmodule
